# Fritzing sketch ToneKeyboardLED (saved by Fritzing 0.9.3b)
breadboards: 1

parts:
  Part1 = Arduino Uno (Rev3)
  LED1 = LED - 5mm [color="Red (633nm)" package="5 mm [THT]"]
  R1 = Resistor [tolerance=±5% resistance=220 package=THT]
  J1 = Basic Force Sensing Resistor (FSR) [package=THT]
  R2 = Resistor [tolerance=±5% resistance=220 package=THT]
  SP1 = SPEAKER [package=pcb_mount_speaker]
  R3 = Resistor [tolerance=±5% resistance=220 package="0805 [SMD]"]

nets:
  N1: Part1.A0, R1.Pin_0, J1.pin_0
  N2: Part1.D8, R2.Pin_0
  N3: Part1.D12/MISO, LED1.anode
  N4: Part1.5V, J1.pin_1, R3.Pin_1
  N5: Part1.GND, R1.Pin_1, SP1.+
  N6: LED1.cathode, R3.Pin_0
  N7: R2.Pin_1, SP1.-
